// Logisim project NewCacheMemory.circ as structural Verilog: 1 circuit, main circuit newMemory
module newMemory (
  input  [31:0] MemAddress,
  input  [31:0] MemWriteData,
  input  clk,
  output miss,
  output [31:0] result
);

  wire undriven_2, undriven_3, write0, write1, write2, write3;
  wire [1:0] memdelayed_1_p5, undriven;
  wire [31:0] cache_1_w0, cache_1_w1, cache_1_w2, cache_1_w3, demultiplexer_1_out0, demultiplexer_1_out1,
       demultiplexer_1_out2, demultiplexer_1_out3, memdelayed_1_p4, multiplexer_1_out, multiplexer_2_out,
       multiplexer_3_out, multiplexer_4_out, multiplexer_5_out, register_1_q, register_2_q, register_3_q,
       register_4_q, w0, w1, w2, w3;

  Multiplexer #(.select(2), .width(32)) multiplexer_1 (
    .in0(w0), .in1(w1), .in2(w2), .in3(w3), .out(multiplexer_1_out), .sel(undriven));
  // memDelayed memdelayed_1: pin names not known; wires that end beside it: MemAddress, 4'b1111, multiplexer_1_out, memdelayed_1_p4, memdelayed_1_p5
  Demultiplexer #(.select(2), .width(32)) demultiplexer_1 (
    .out0(demultiplexer_1_out0), .out1(demultiplexer_1_out1), .out2(demultiplexer_1_out2),
    .out3(demultiplexer_1_out3), .in(memdelayed_1_p4), .sel(memdelayed_1_p5));
  Demultiplexer #(.enable("true"), .select(2)) demultiplexer_2 (
    .out0(write0), .out1(write1), .out2(write2), .out3(write3), .in(1'b1), .sel(MemAddress[1:0]),
    .en(undriven_2));
  Register #(.width(32)) register_1 (.D(demultiplexer_1_out0), .Q(register_1_q));  // open: en, clk, clr
  Register #(.width(32)) register_2 (.D(demultiplexer_1_out1), .Q(register_2_q));  // open: en, clk, clr
  Register #(.width(32)) register_3 (.D(demultiplexer_1_out3), .Q(register_3_q));  // open: en, clk, clr
  Register #(.width(32)) register_4 (.D(demultiplexer_1_out2), .Q(register_4_q));  // open: en, clk, clr
  Multiplexer #(.width(32)) multiplexer_2 (
    .in0(register_1_q), .in1(MemWriteData), .out(multiplexer_2_out), .sel(write0));
  Multiplexer #(.width(32)) multiplexer_3 (
    .in0(register_2_q), .in1(MemWriteData), .out(multiplexer_3_out), .sel(write1));
  Multiplexer #(.width(32)) multiplexer_4 (
    .in0(register_4_q), .in1(MemWriteData), .out(multiplexer_4_out), .sel(write2));
  Multiplexer #(.width(32)) multiplexer_5 (
    .in0(register_3_q), .in1(MemWriteData), .out(multiplexer_5_out), .sel(write3));
  Cache cache_1 (
    .W0_write(multiplexer_2_out), .W1_write(multiplexer_3_out), .W2_write(multiplexer_4_out),
    .W3_write(multiplexer_5_out), .Tag_writeAndRead(MemAddress[13:4]), .word_read(MemAddress[1:0]),
    .SetBit_writeAndRead(MemAddress[3:2]), .multipleSingleNot(undriven_3), .miss(miss), .BlockWord(result),
    .w0(cache_1_w0), .w1(cache_1_w1), .w2(cache_1_w2), .w3(cache_1_w3));  // open: clk, throwTag
  Register #(.width(32)) register_5 (.D(cache_1_w0), .Q(w0));  // open: en, clk, clr
  Register #(.width(32)) register_6 (.D(cache_1_w1), .Q(w1));  // open: en, clk, clr
  Register #(.width(32)) register_7 (.D(cache_1_w2), .Q(w2));  // open: en, clk, clr
  Register #(.width(32)) register_8 (.D(cache_1_w3), .Q(w3));  // open: en, clk, clr

  // Other names for the same wires on the sheet: address[31:0] = MemAddress; word[1:0] = MemAddress[1:0];
  //   set[1:0] = MemAddress[3:2]; tag[9:0] = MemAddress[13:4]; writeData[31:0] = MemWriteData

  // Notes on the sheet:
  //   single or block
  //   change whether single write or block write
endmodule
