// Logisim project au.circ as structural Verilog: 3 circuits, main circuit ALU
module ALU (
  input  [31:0] rs,
  input  [31:0] rt,
  input  [31:0] imm,
  input  [4:0] shiftAmount,
  input  [5:0] opcode,
  input  [5:0] func,
  input  SaturationBit,
  output [31:0] result,
  output zero,
  output [1:0] PCcontrol,
  output SatuControll
);

  wire BEQ, BGEZ, BGTZ, BLEZ, BNE, comparator_1_eq, comparator_1_gt, comparator_3_gt, comparator_3_lt,
       comparator_4_eq, comparator_4_lt, comparator_6_lt, comparator_7_lt, isJrOn, isR, jmpadd, jmpimm,
       jmpreg, nor_2_out;
  wire [31:0] ADD, ADDi, ADDu, ADDui, AND0, ANDi, DIV, LUI, MEMADD, MULT, multiplexer_1_out, NOR0, OR0, ORi,
       Rformat, SLL0, SLLV0, SLT, SLTi, SRA0, SRL0, SRLV0, SUB, SUBu, SYS, XOR0, XORi;

  Comparator #(.width(32)) comparator_1 (
    .a(rs), .b({32{1'b0}}), .gt(comparator_1_gt), .eq(comparator_1_eq));  // open: lt
  Comparator #(.width(32)) comparator_2 (.a(rs), .b(rt), .eq(BEQ));  // open: gt, lt
  Comparator #(.width(32)) comparator_3 (.a(rs), .b(rt), .gt(comparator_3_gt), .lt(comparator_3_lt));  // open: eq
  Comparator #(.width(32)) comparator_4 (
    .a(rs), .b({32{1'b0}}), .eq(comparator_4_eq), .lt(comparator_4_lt));  // open: gt
  Comparator #(.width(32)) comparator_5 (.a(rs), .b({32{1'b0}}), .gt(BGTZ));  // open: eq, lt
  Shifter #(.width(32)) shifter_1 (.in(imm), .\dist (5'b10000), .out(LUI));
  Adder #(.width(32)) adder_1 (.a(imm), .b(rs), .out(MEMADD));  // open: cin, cout
  or or_1 (BGEZ, comparator_1_gt, comparator_1_eq);
  or or_2 (BNE, comparator_3_gt, comparator_3_lt);
  or or_3 (BLEZ, comparator_4_eq, comparator_4_lt);
  Comparator #(.width(32)) comparator_6 (.a(rs), .b(rt), .lt(comparator_6_lt));  // open: gt, eq
  Comparator #(.width(32)) comparator_7 (.a(rs), .b(imm), .lt(comparator_7_lt));  // open: gt, eq
  Adder #(.width(32)) adder_2 (.a(rs), .b(rt), .out(ADD));  // open: cin, cout
  Adder #(.width(32)) adder_3 (.a(rs), .b(rt), .out(ADDu));  // open: cin, cout
  Subtractor #(.width(32)) subtractor_1 (.a(rs), .b(rt), .out(SUB));  // open: bin, bout
  Subtractor #(.width(32)) subtractor_2 (.a(rs), .b(rt), .out(SUBu));  // open: bin, bout
  assign XOR0 = rs ^ rt;  // XOR_Gate xor_1, 32 bits wide
  assign AND0 = rs & rt;  // AND_Gate and_1, 32 bits wide
  assign OR0 = rs | rt;  // OR_Gate or_4, 32 bits wide
  assign NOR0 = ~(rs | rt);  // NOR_Gate nor_1, 32 bits wide
  Multiplier #(.width(32)) multiplier_1 (.a(rs), .b(rt), .out(MULT));  // open: cin, cout
  Divider #(.width(32)) divider_1 (.a(rs), .b(rt), .out(DIV));  // open: upper, rem
  Shifter #(.width(32)) shifter_2 (.in(rt), .\dist (shiftAmount), .out(SLL0));
  Shifter #(.width(32)) shifter_3 (.in(rt), .\dist (rs[4:0]), .out(SLLV0));
  Shifter #(.shift("lr"), .width(32)) shifter_4 (.in(rt), .\dist (shiftAmount), .out(SRL0));
  Shifter #(.shift("lr"), .width(32)) shifter_5 (.in(rt), .\dist (rs[4:0]), .out(SRLV0));
  Shifter #(.shift("ar"), .width(32)) shifter_6 (.in(rt), .\dist (shiftAmount), .out(SRA0));
  assign SLT = {{31{1'b0}}, comparator_6_lt};  // Bit_Extender bit_extender_1
  Adder #(.width(32)) adder_4 (.a(rs), .b(imm), .out(ADDi));  // open: cin, cout
  Adder #(.width(32)) adder_5 (.a(rs), .b(imm), .out(ADDui));  // open: cin, cout
  assign SLTi = {{31{1'b0}}, comparator_7_lt};  // Bit_Extender bit_extender_2
  assign XORi = rs ^ imm;  // XOR_Gate xor_2, 32 bits wide
  assign ANDi = rs & imm;  // AND_Gate and_2, 32 bits wide
  assign ORi = rs | imm;  // OR_Gate or_5, 32 bits wide
  Multiplexer #(.width(32)) multiplexer_1 (.in0(rs), .in1(MULT), .out(multiplexer_1_out), .sel(func[4]));
  Multiplexer #(.select(5)) multiplexer_2 (
    .in0(1'b0), .in1(BGEZ), .in2(1'b0), .in3(1'b0), .in4(BEQ), .in5(BNE), .in6(BLEZ), .in7(BGTZ), .in8(1'b0),
    .in9(1'b0), .in10(1'b0), .in11(1'b0), .in12(1'b0), .in13(1'b0), .in14(1'b0), .in15(1'b0), .in16(1'b0),
    .in17(1'b0), .in18(1'b0), .in19(1'b0), .in20(1'b0), .in21(1'b0), .in22(1'b0), .in23(1'b0), .in24(1'b0),
    .in25(1'b0), .in26(1'b0), .in27(1'b0), .in28(1'b0), .in29(1'b0), .in30(1'b0), .in31(1'b0), .out(jmpimm),
    .sel({opcode[5], opcode[3:0]}));
  or or_6 (isR, opcode[0], opcode[1], opcode[2], opcode[3], opcode[4], opcode[5]);
  nor nor_2 (nor_2_out, jmpimm, jmpreg, jmpadd);
  or or_7 (SatuControll, jmpimm, jmpreg, jmpadd);
  Multiplexer #(.select(5)) multiplexer_3 (
    .in0(1'b0), .in1(1'b0), .in2(1'b1), .in3(1'b1), .in4(1'b0), .in5(1'b0), .in6(1'b0), .in7(1'b0),
    .in8(1'b0), .in9(1'b0), .in10(1'b0), .in11(1'b0), .in12(1'b0), .in13(1'b0), .in14(1'b0), .in15(1'b0),
    .in16(1'b0), .in17(1'b0), .in18(1'b0), .in19(1'b0), .in20(1'b0), .in21(1'b0), .in22(1'b0), .in23(1'b0),
    .in24(1'b0), .in25(1'b0), .in26(1'b0), .in27(1'b0), .in28(1'b0), .in29(1'b0), .in30(1'b0), .in31(1'b0),
    .out(jmpadd), .sel({opcode[5], opcode[3:0]}));
  and and_3 (jmpreg, isJrOn, isR);
  Multiplexer #(.select(5), .width(32)) multiplexer_4 (
    .in0(SLL0), .in2(SRL0), .in3(SRA0), .in4(SLLV0), .in6(SRLV0), .in8(multiplexer_1_out), .in10(DIV),
    .in12(SYS), .in16(ADD), .in17(ADDu), .in18(SUB), .in19(SUBu), .in20(AND0), .in21(OR0), .in22(XOR0),
    .in23(NOR0), .in26(SLT), .out(Rformat), .sel({func[5], func[3:0]}));  // open: in1, in5, in7, in9, in11, in13, in14, in15, in24, in25, in27, in28, in29, in30, in31
  Multiplexer #(.select(5), .width(32)) multiplexer_5 (
    .in0(Rformat), .in1({32{1'b0}}), .in2({32{1'b0}}), .in3({32{1'b0}}), .in4({32{1'b0}}), .in5({32{1'b0}}),
    .in6({32{1'b0}}), .in7({32{1'b0}}), .in8(ADDi), .in9(ADDui), .in10(SLTi), .in11({32{1'b0}}), .in12(ANDi),
    .in13(ORi), .in14(XORi), .in15(LUI), .in16(MEMADD), .in17({32{1'b0}}), .in18({32{1'b0}}), .in19(MEMADD),
    .in20({32{1'b0}}), .in21({32{1'b0}}), .in22({32{1'b0}}), .in23({32{1'b0}}), .in24(MEMADD),
    .in25({32{1'b0}}), .in26({32{1'b0}}), .in27(MEMADD), .in28({32{1'b0}}), .in29({32{1'b0}}),
    .in30({32{1'b0}}), .in31({32{1'b0}}), .out(result), .sel({opcode[5], opcode[3:0]}));
  Multiplexer #(.select(5)) multiplexer_6 (
    .in0(1'b0), .in1(1'b0), .in2(1'b0), .in3(1'b0), .in4(1'b0), .in5(1'b0), .in6(1'b0), .in7(1'b0),
    .in8(func[4]), .in9(1'b0), .in10(1'b0), .in11(1'b0), .in12(1'b0), .in13(1'b0), .in14(1'b0), .in15(1'b0),
    .in16(1'b0), .in17(1'b0), .in18(1'b0), .in19(1'b0), .in20(1'b0), .in21(1'b0), .in22(1'b0), .in23(1'b0),
    .in24(1'b0), .in25(1'b0), .in26(1'b0), .in27(1'b0), .in28(1'b0), .in29(1'b0), .in30(1'b0), .in31(1'b0),
    .out(isJrOn), .sel({func[5], func[3:0]}));
  Priority_Encoder #(.select(2)) priority_encoder_1 (
    .in0(nor_2_out), .in1(jmpimm), .in2(jmpreg), .in3(jmpadd), .out(PCcontrol));  // open: gs, en_out, en_in

  // Other names for the same wires on the sheet: FromSat = SaturationBit; OP[5:0] = opcode; PC[1:0] = PCcontrol;
  //   reg1[31:0] = rs; reg2[31:0] = rt; SA[4:0] = shiftAmount; SatuControl = SatuControll

  // Notes on the sheet:
  //   inputs
  //   outputs
endmodule

module ALU_Control (
  input  [31:0] reg1,
  input  [31:0] reg2,
  input  [4:0] shiftAmount,
  input  [5:0] opcode,
  input  [5:0] func,
  output isRes,
  output isJAL,
  output isWriteRD,
  output syscall,
  output [3:0] Byte,
  output WriteReg
);

  wire and_1_out, nand_1_out, nor_2_out, not_1_out, not_2_out, not_3_out, not_4_out, not_5_out, not_6_out,
       not_7_out, not_8_out, not_9_out, not_10_out, not_11_out, not_12_out, not_13_out, not_14_out,
       not_15_out, not_16_out, not_17_out, xnor_1_out;

  not not_1 (not_1_out, func[0]);
  not not_2 (not_2_out, func[1]);
  not not_3 (not_3_out, func[2]);
  not not_4 (not_4_out, func[4]);
  not not_5 (not_5_out, func[5]);
  nand nand_1 (nand_1_out, not_1_out, not_2_out, not_3_out, func[3], not_4_out, not_5_out);
  not not_6 (not_6_out, opcode[2]);
  not not_7 (not_7_out, opcode[3]);
  not not_8 (not_8_out, opcode[4]);
  not not_9 (not_9_out, opcode[2]);
  not not_10 (not_10_out, opcode[3]);
  not not_11 (not_11_out, opcode[4]);
  not not_12 (not_12_out, opcode[5]);
  not not_13 (not_13_out, opcode[5]);
  xnor xnor_1 (xnor_1_out, opcode[0], opcode[1]);
  not not_14 (not_14_out, func[0]);
  not not_15 (not_15_out, func[1]);
  not not_16 (not_16_out, func[4]);
  not not_17 (not_17_out, func[5]);
  nor nor_1 (isWriteRD, opcode[0], opcode[1], opcode[2], opcode[3], opcode[4], opcode[5]);
  and and_1 (and_1_out, not_14_out, not_15_out, func[2], func[3], not_16_out, not_17_out);
  and and_2 (isRes, xnor_1_out, not_6_out, not_7_out, not_8_out, opcode[5]);
  and and_3 (isJAL, opcode[0], opcode[1], not_9_out, not_10_out, not_11_out, not_12_out);
  nor nor_2 (nor_2_out, opcode[0], opcode[1], opcode[2], opcode[3], opcode[4], not_13_out);
  Multiplexer #(.width(4)) multiplexer_1 (.in0(4'b1111), .in1(4'b0001), .out(Byte), .sel(nor_2_out));
  and and_4 (syscall, isWriteRD, and_1_out);
  Multiplexer #(.select(5)) multiplexer_2 (
    .in0(nand_1_out), .in1(1'b0), .in2(1'b0), .in3(1'b0), .in4(1'b0), .in5(1'b0), .in6(1'b0), .in7(1'b0),
    .in8(1'b1), .in9(1'b1), .in10(1'b1), .in11(1'b0), .in12(1'b1), .in13(1'b1), .in14(1'b1), .in15(1'b1),
    .in16(1'b1), .in17(1'b0), .in18(1'b0), .in19(1'b1), .in20(1'b0), .in21(1'b0), .in22(1'b0), .in23(1'b0),
    .in24(1'b0), .in25(1'b0), .in26(1'b0), .in27(1'b0), .in28(1'b0), .in29(1'b0), .in30(1'b0), .in31(1'b0),
    .out(WriteReg), .sel({opcode[5], opcode[3:0]}));

  // Other names for the same wires on the sheet: OP[5:0] = opcode; SA[4:0] = shiftAmount

  // Notes on the sheet:
  //   inputs
  //   outputs
endmodule

module JumpController (
  input  [5:0] opcode,
  input  SatuBit,
  output [1:0] PCcontrol
);

  wire and_1_out, jmpadd, jmpimm, nor_1_out, not_1_out, or_1_out;

  Multiplexer #(.select(5)) multiplexer_1 (
    .in0(1'b0), .in1(1'b1), .in2(1'b0), .in3(1'b0), .in4(1'b1), .in5(1'b1), .in6(1'b1), .in7(1'b1),
    .in8(1'b0), .in9(1'b0), .in10(1'b0), .in11(1'b0), .in12(1'b0), .in13(1'b0), .in14(1'b0), .in15(1'b0),
    .in16(1'b0), .in17(1'b0), .in18(1'b0), .in19(1'b0), .in20(1'b0), .in21(1'b0), .in22(1'b0), .in23(1'b0),
    .in24(1'b0), .in25(1'b0), .in26(1'b0), .in27(1'b0), .in28(1'b0), .in29(1'b0), .in30(1'b0), .in31(1'b0),
    .out(jmpimm), .sel({opcode[5], opcode[3:0]}));
  nor nor_1 (nor_1_out, jmpimm, 1'b0, jmpadd);
  not not_1 (not_1_out, nor_1_out);
  Multiplexer #(.select(5)) multiplexer_2 (
    .in0(1'b0), .in1(1'b0), .in2(1'b1), .in3(1'b1), .in4(1'b0), .in5(1'b0), .in6(1'b0), .in7(1'b0),
    .in8(1'b0), .in9(1'b0), .in10(1'b0), .in11(1'b0), .in12(1'b0), .in13(1'b0), .in14(1'b0), .in15(1'b0),
    .in16(1'b0), .in17(1'b0), .in18(1'b0), .in19(1'b0), .in20(1'b0), .in21(1'b0), .in22(1'b0), .in23(1'b0),
    .in24(1'b0), .in25(1'b0), .in26(1'b0), .in27(1'b0), .in28(1'b0), .in29(1'b0), .in30(1'b0), .in31(1'b0),
    .out(jmpadd), .sel({opcode[5], opcode[3:0]}));
  and and_1 (and_1_out, SatuBit, not_1_out);
  or or_1 (or_1_out, and_1_out, nor_1_out);
  Priority_Encoder #(.select(2)) priority_encoder_1 (
    .in0(or_1_out), .in1(jmpimm), .in2(1'b0), .in3(jmpadd), .out(PCcontrol));  // open: gs, en_out, en_in

  // Other names for the same wires on the sheet: OP[5:0] = opcode; PC[1:0] = PCcontrol

  // Notes on the sheet:
  //   inputs
endmodule
