// Logisim project bitExtender.circ as structural Verilog: 1 circuit, main circuit bitExtender
module bitExtender (
  input  [15:0] inbit,
  output [31:0] outbit
);


  assign outbit = {{17{inbit[15]}}, inbit[14:0]};
endmodule
