// Logisim project cacheMemory.circ as structural Verilog: 3 circuits, main circuit Cache
module Cache (
  input  [31:0] W0_write,
  input  [31:0] W1_write,
  input  [31:0] W2_write,
  input  [31:0] W3_write,
  input  [9:0] Tag_writeAndRead,
  input  clk,
  input  [1:0] word_read,
  input  [1:0] SetBit_writeAndRead,
  input  multipleSingleNot,
  output miss,
  output [31:0] BlockWord,
  output [9:0] throwTag,
  output [31:0] w0,
  output [31:0] w1,
  output [31:0] w2,
  output [31:0] w3
);

  wire demultiplexer_1_out0, demultiplexer_1_out1, demultiplexer_1_out2, demultiplexer_1_out3, set_1_miss,
       set_2_miss, set_3_miss, set_4_miss;
  wire [9:0] set_1_throwtag, set_2_throwtag, set_3_throwtag, set_4_throwtag;
  wire [31:0] set_1_blockword, set_2_blockword, set_3_blockword, set_4_blockword, w00, w01, w02, w03, w10,
       w11, w12, w13, w20, w21, w22, w23, w30, w31, w32, w33;

  Demultiplexer #(.select(2)) demultiplexer_1 (
    .out0(demultiplexer_1_out0), .out1(demultiplexer_1_out1), .out2(demultiplexer_1_out2),
    .out3(demultiplexer_1_out3), .in(1'b1), .sel(SetBit_writeAndRead));
  SET set_1 (
    .W0_write(W0_write), .W1_write(W1_write), .W2_write(W2_write), .W3_write(W3_write), .clk(clk),
    .Word_read(word_read), .Tag_writeAndRead(Tag_writeAndRead), .writeEnable(demultiplexer_1_out0),
    .multipleSingleNot(multipleSingleNot), .BlockWord(set_1_blockword), .miss(set_1_miss), .w0(w00),
    .w1(w01), .w2(w02), .w3(w03), .throwTag(set_1_throwtag));
  SET set_2 (
    .W0_write(W0_write), .W1_write(W1_write), .W2_write(W2_write), .W3_write(W3_write), .clk(clk),
    .Word_read(word_read), .Tag_writeAndRead(Tag_writeAndRead), .writeEnable(demultiplexer_1_out1),
    .multipleSingleNot(multipleSingleNot), .BlockWord(set_2_blockword), .miss(set_2_miss), .w0(w10),
    .w1(w11), .w2(w12), .w3(w13), .throwTag(set_2_throwtag));
  SET set_3 (
    .W0_write(W0_write), .W1_write(W1_write), .W2_write(W2_write), .W3_write(W3_write), .clk(clk),
    .Word_read(word_read), .Tag_writeAndRead(Tag_writeAndRead), .writeEnable(demultiplexer_1_out2),
    .multipleSingleNot(multipleSingleNot), .BlockWord(set_3_blockword), .miss(set_3_miss), .w0(w20),
    .w1(w21), .w2(w22), .w3(w23), .throwTag(set_3_throwtag));
  SET set_4 (
    .W0_write(W0_write), .W1_write(W1_write), .W2_write(W2_write), .W3_write(W3_write), .clk(clk),
    .Word_read(word_read), .Tag_writeAndRead(Tag_writeAndRead), .writeEnable(demultiplexer_1_out3),
    .multipleSingleNot(multipleSingleNot), .BlockWord(set_4_blockword), .miss(set_4_miss), .w0(w30),
    .w1(w31), .w2(w32), .w3(w33), .throwTag(set_4_throwtag));
  Multiplexer #(.select(2), .width(32)) multiplexer_1 (
    .in0(set_1_blockword), .in1(set_2_blockword), .in2(set_3_blockword), .in3(set_4_blockword),
    .out(BlockWord), .sel(SetBit_writeAndRead));
  Multiplexer #(.select(2), .width(10)) multiplexer_2 (
    .in0(set_1_throwtag), .in1(set_2_throwtag), .in2(set_3_throwtag), .in3(set_4_throwtag), .out(throwTag),
    .sel(SetBit_writeAndRead));
  or or_1 (miss, set_1_miss, set_2_miss, set_3_miss, set_4_miss);
  Multiplexer #(.select(2), .width(32)) multiplexer_3 (
    .in0(w00), .in1(w10), .in2(w20), .in3(w30), .out(w0), .sel(SetBit_writeAndRead));
  Multiplexer #(.select(2), .width(32)) multiplexer_4 (
    .in0(w01), .in1(w11), .in2(w21), .in3(w31), .out(w1), .sel(SetBit_writeAndRead));
  Multiplexer #(.select(2), .width(32)) multiplexer_5 (
    .in0(w02), .in1(w12), .in2(w22), .in3(w32), .out(w2), .sel(SetBit_writeAndRead));
  Multiplexer #(.select(2), .width(32)) multiplexer_6 (
    .in0(w03), .in1(w13), .in2(w23), .in3(w33), .out(w3), .sel(SetBit_writeAndRead));

  // Other names for the same wires on the sheet: msn = multipleSingleNot; tag[9:0] = Tag_writeAndRead;
  //   W0_t[31:0] = W0_write; W1_t[31:0] = W1_write; W2_t[31:0] = W2_write; W3_t[31:0] = W3_write;
  //   word[1:0] = word_read
endmodule

module BLOCK_4x32 (
  input  [31:0] W0_write,
  input  [31:0] W1_write,
  input  [31:0] W2_write,
  input  [31:0] W3_write,
  input  clk,
  input  [1:0] Word_read,
  input  [9:0] Tag_write,
  input  V,
  input  Enable,
  input  multipleSingleNot,
  output [31:0] w0,
  output [31:0] w1,
  output [31:0] w2,
  output [31:0] w3,
  output [31:0] BlockWord,
  output [9:0] BlockTag,
  output validBit
);

  wire demultiplexer_1_out0, demultiplexer_1_out1, demultiplexer_1_out2, demultiplexer_1_out3,
       multiplexer_1_out, multiplexer_2_out, multiplexer_3_out, multiplexer_4_out;

  Demultiplexer #(.select(2)) demultiplexer_1 (
    .out0(demultiplexer_1_out0), .out1(demultiplexer_1_out1), .out2(demultiplexer_1_out2),
    .out3(demultiplexer_1_out3), .in(Enable), .sel(Word_read));
  Register #(.width(32)) register_1 (.D(W0_write), .en(multiplexer_1_out), .clk(clk), .Q(w0));  // open: clr
  Multiplexer multiplexer_1 (
    .in0(Enable), .in1(demultiplexer_1_out0), .out(multiplexer_1_out), .sel(multipleSingleNot));
  Register #(.width(32)) register_2 (.D(W1_write), .en(multiplexer_2_out), .clk(clk), .Q(w1));  // open: clr
  Multiplexer multiplexer_2 (
    .in0(Enable), .in1(demultiplexer_1_out1), .out(multiplexer_2_out), .sel(multipleSingleNot));
  Register #(.width(32)) register_3 (.D(W2_write), .en(multiplexer_3_out), .clk(clk), .Q(w2));  // open: clr
  Multiplexer multiplexer_3 (
    .in0(Enable), .in1(demultiplexer_1_out2), .out(multiplexer_3_out), .sel(multipleSingleNot));
  Register #(.width(32)) register_4 (.D(W3_write), .en(multiplexer_4_out), .clk(clk), .Q(w3));  // open: clr
  Multiplexer multiplexer_4 (
    .in0(Enable), .in1(demultiplexer_1_out3), .out(multiplexer_4_out), .sel(multipleSingleNot));
  Register #(.width(10)) register_5 (.D(Tag_write), .en(Enable), .clk(clk), .Q(BlockTag));  // open: clr
  Register #(.width(1)) register_6 (.D(V), .en(Enable), .clk(clk), .Q(validBit));  // open: clr
  Multiplexer #(.select(2), .width(32)) multiplexer_5 (
    .in0(w0), .in1(w1), .in2(w2), .in3(w3), .out(BlockWord), .sel(Word_read));

  // Other names for the same wires on the sheet: msn = multipleSingleNot

  // Notes on the sheet:
  //   when enable is 1 and v is 1 we should write back in memory
endmodule

module SET (
  input  [31:0] W0_write,
  input  [31:0] W1_write,
  input  [31:0] W2_write,
  input  [31:0] W3_write,
  input  clk,
  input  [1:0] Word_read,
  input  [9:0] Tag_writeAndRead,
  input  writeEnable,
  input  multipleSingleNot,
  output [31:0] BlockWord,
  output miss,
  output [31:0] w0,
  output [31:0] w1,
  output [31:0] w2,
  output [31:0] w3,
  output [9:0] throwTag
);

  wire and_1_out, and_2_out, and_3_out, clk_t, comparator_1_eq, comparator_2_eq, enable, not_1_out, v1, v2;
  wire [9:0] blockTag1, blockTag2, firstRecentTag_q, secondRecentTag_q;
  wire [31:0] block_4x32_1_blockword, block_4x32_2_blockword, w00, w01, w02, w03, w10, w11, w12, w13;

  and and_1 (and_1_out, clk, miss);
  Register #(.width(10)) firstRecentTag (.D(Tag_writeAndRead), .clk(and_1_out), .Q(firstRecentTag_q));  // open: en, clr
  Multiplexer multiplexer_1 (.in0(1'b0), .in1(clk), .out(clk_t), .sel(writeEnable));
  Register #(.width(10)) secondRecentTag (
    .D(firstRecentTag_q), .clk(and_1_out), .Q(secondRecentTag_q));  // open: en, clr
  not not_1 (not_1_out, enable);
  Register #(.width(10)) thirdRecentTag (.D(secondRecentTag_q), .clk(and_1_out), .Q(throwTag));  // open: en, clr
  BLOCK_4x32 block_4x32_1 (
    .W0_write(W0_write), .W1_write(W1_write), .W2_write(W2_write), .W3_write(W3_write), .clk(clk_t),
    .Word_read(Word_read), .Tag_write(Tag_writeAndRead), .V(1'b1), .Enable(enable),
    .multipleSingleNot(multipleSingleNot), .w0(w00), .w1(w01), .w2(w02), .w3(w03),
    .BlockWord(block_4x32_1_blockword), .BlockTag(blockTag1), .validBit(v1));
  BLOCK_4x32 block_4x32_2 (
    .W0_write(W0_write), .W1_write(W1_write), .W2_write(W2_write), .W3_write(W3_write), .clk(clk_t),
    .Word_read(Word_read), .Tag_write(Tag_writeAndRead), .V(1'b1), .Enable(not_1_out),
    .multipleSingleNot(multipleSingleNot), .w0(w10), .w1(w11), .w2(w12), .w3(w13),
    .BlockWord(block_4x32_2_blockword), .BlockTag(blockTag2), .validBit(v2));
  Comparator #(.width(10)) comparator_1 (.a(blockTag1), .b(Tag_writeAndRead), .eq(comparator_1_eq));  // open: gt, lt
  Comparator #(.width(10)) comparator_2 (.a(Tag_writeAndRead), .b(blockTag2), .eq(comparator_2_eq));  // open: gt, lt
  Comparator #(.width(10)) comparator_3 (.a(throwTag), .b(blockTag1), .eq(enable));  // open: gt, lt
  and and_2 (and_2_out, v1, comparator_1_eq);
  and and_3 (and_3_out, comparator_2_eq, v2);
  Multiplexer #(.enable("true"), .width(32)) multiplexer_2 (
    .in0(block_4x32_1_blockword), .in1(block_4x32_2_blockword), .out(BlockWord), .sel(and_3_out), .en(miss));
  nor nor_1 (miss, and_2_out, and_3_out);
  Multiplexer #(.width(32)) multiplexer_3 (.in0(w10), .in1(w00), .out(w0), .sel(enable));
  Multiplexer #(.width(32)) multiplexer_4 (.in0(w11), .in1(w01), .out(w1), .sel(enable));
  Multiplexer #(.width(32)) multiplexer_5 (.in0(w12), .in1(w02), .out(w2), .sel(enable));
  Multiplexer #(.width(32)) multiplexer_6 (.in0(w13), .in1(w03), .out(w3), .sel(enable));

  // Other names for the same wires on the sheet: clkMain = clk; msn = multipleSingleNot; tag[9:0] = Tag_writeAndRead;
  //   W0_t[31:0] = W0_write; W1_t[31:0] = W1_write; W2_t[31:0] = W2_write; W3_t[31:0] = W3_write;
  //   word[1:0] = Word_read

  // Notes on the sheet:
  //   this clock only activates for write
  //   if 1 miss
endmodule
