// Logisim project cpu.circ as structural Verilog: 3 circuits, main circuit cpu
module cpu (
  input  in_1,
  input  in_2,
  input  in_3,
  input  in_4
);

  wire comparator_1_eq, d_ff_1_q, d_ff_2_q, ForceStop, isJAL_1, isJAL_2, isJAL_3, isRes_1, isRes_2, isRes_3,
       isSATequalPC, isWriteRD_1, isWriteRD_2, isWriteRD_3, not_1_out, not_2_out, not_3_out, or_1_out,
       Satu_1, SatuBit, saturationcounter_1_t1, syscall, syscall_1, syscall_2, syscall_3, WriteReg_1,
       WriteReg_2, WriteReg_3, zero_1;
  wire [1:0] PCcontrol_1, PCcontrol_2, SATPCcontrol;
  wire [3:0] Byte_1, Byte_2, Byte_3;
  wire [4:0] multiplexer_3_out, multiplexer_4_out;
  wire [25:0] ADD, ADD_0, ADD_1, ADD_2, ADD_3;
  wire [31:0] adder_1_out, adder_3_out, DataMem_p5, imm32, imm32_0, imm32_1, imm32_2, imm32_3,
       multiplexer_1_out, multiplexer_5_out, nPC, nPC_1, PC, PC4, PC4_0, PC4_1, PC4_2, PC4_3, PC_0, PC_1,
       PC_2, res_1, res_2, rsdata, rsdata_1, rtdata, rtdata_1, rtdata_2, satPC, satPC_0, satPC_1,
       shifter_1_out, shifter_2_out, writedata_2, writedata_3;
  wire [31:26] INS, INS_0, INS_1, INS_2, INS_3;

  Shifter #(.width(32)) shifter_1 (.in(imm32_0), .\dist (5'b00010), .out(shifter_1_out));
  Multiplexer #(.width(32)) multiplexer_1 (.in0(nPC), .in1(satPC), .out(multiplexer_1_out), .sel(isSATequalPC));
  Adder #(.width(32)) adder_1 (.a(PC4), .b(shifter_1_out), .out(adder_1_out));  // open: cin, cout
  Register #(.width(32)) u_PC (.D(multiplexer_1_out), .en(not_1_out), .clk(in_2), .Q(PC));  // open: clr
  not not_1 (not_1_out, syscall);
  Adder #(.width(32)) adder_2 (.a(PC), .b(32'h4), .out(PC4));  // open: cin, cout
  // mem InstMem: pin names not known; wires that end beside it: PC, 4'b0000, {32{1'b0}}, in_2, {INS_0, ADD_0}
  Multiplexer #(.select(2), .width(32)) multiplexer_2 (
    .in0(PC4), .in1(adder_1_out), .in3({PC[31:28], ADD_0, 2'b00}), .out(satPC), .sel(SATPCcontrol));  // open: in2
  JumpController jumpcontroller_1 (.opcode(INS_0), .SatuBit(SatuBit), .PCcontrol(SATPCcontrol));
  BigBuffer bigbuffer_1 (
    .In32_1({INS_0, ADD_0}), .In32_2(PC4), .In32_3(PC), .In16_2(satPC), .clk(in_2), .Out32_1({INS, ADD}),
    .Out32_2(PC4_0), .Out32_3(PC_0), .Out16_2(satPC_0));  // open: In32_4, In32_5, In1_1, In1_2, In1_3, In1_4, In4_1, In1_6, In1_7, In1_8, In1_9, In1_10, In1_11, In2_1, stop, Out32_4, Out32_5, Out1_1, Out1_2, Out1_3, Out1_4, Out4_1, Out1_6, Out1_7, Out1_8, Out1_9, Out1_10, Out1_11, Out2_1
  assign imm32 = {{16{ADD[15]}}, ADD[15:0]};  // Bit_Extender bit_extender_1
  Multiplexer #(.width(5)) multiplexer_3 (
    .in0(ADD_3[20:16]), .in1(ADD_3[15:11]), .out(multiplexer_3_out), .sel(isWriteRD_3));
  Multiplexer #(.width(5)) multiplexer_4 (
    .in0(multiplexer_3_out), .in1({5{1'b1}}), .out(multiplexer_4_out), .sel(isJAL_3));
  assign imm32_1 = {{16{ADD_1[15]}}, ADD_1[15:0]};  // Bit_Extender bit_extender_2
  Multiplexer #(.width(32)) multiplexer_5 (.in0(writedata_3), .in1(PC4_3), .out(multiplexer_5_out), .sel(isJAL_3));
  fiveCounter fivecounter_1 (.Start(in_1), .Clk(in_3), .miss(in_4));  // open: S_IF, S_ID, S_EX, S_MEM, S_WB
  assign imm32_3 = {{16{ADD_3[15]}}, ADD_3[15:0]};  // Bit_Extender bit_extender_3
  // regfile RegisterFile: pin names not known; wires that end beside it: ADD[25:21], ADD[20:16], multiplexer_4_out, multiplexer_5_out, WriteReg_3, in_2, rsdata, rtdata
  assign imm32_2 = {{16{ADD_2[15]}}, ADD_2[15:0]};  // Bit_Extender bit_extender_4
  BigBuffer bigbuffer_2 (
    .In32_1({INS, ADD}), .In32_2(PC4_0), .In32_3(rsdata), .In32_4(rtdata), .In32_5(PC_0), .In16_2(satPC_0),
    .clk(in_2), .Out32_1({INS_1, ADD_1}), .Out32_2(PC4_1), .Out32_3(rsdata_1), .Out32_4(rtdata_1),
    .Out32_5(PC_1), .Out16_2(satPC_1));  // open: In1_1, In1_2, In1_3, In1_4, In4_1, In1_6, In1_7, In1_8, In1_9, In1_10, In1_11, In2_1, stop, Out1_1, Out1_2, Out1_3, Out1_4, Out4_1, Out1_6, Out1_7, Out1_8, Out1_9, Out1_10, Out1_11, Out2_1
  not not_2 (not_2_out, Satu_1);
  Adder #(.width(32)) adder_3 (.a(PC4_1), .b(shifter_2_out), .out(adder_3_out));  // open: cin, cout
  Shifter #(.width(32)) shifter_2 (.in(imm32_1), .\dist (5'b00010), .out(shifter_2_out));
  not not_3 (not_3_out, isSATequalPC);
  Comparator #(.width(32)) comparator_1 (.a(satPC_1), .b(nPC), .eq(comparator_1_eq));  // open: gt, lt
  D_Flip_Flop d_ff_1 (.D(or_1_out), .clk(in_2), .Q(d_ff_1_q));  // open: Qn, preset, reset
  or or_1 (or_1_out, in_1, not_3_out);
  ALU alu_1 (
    .rs(rsdata_1), .rt(rtdata_1), .imm(imm32_1), .shiftAmount(ADD_1[10:6]), .opcode(INS_1),
    .func(ADD_1[5:0]), .SaturationBit(SatuBit), .result(res_1), .zero(zero_1), .PCcontrol(PCcontrol_1),
    .SatuControll(Satu_1));
  ALU_Control alu_control_1 (
    .reg1(rsdata_1), .reg2(rtdata_1), .shiftAmount(ADD_1[10:6]), .opcode(INS_1), .func(ADD_1[5:0]),
    .isRes(isRes_1), .isJAL(isJAL_1), .isWriteRD(isWriteRD_1), .syscall(syscall_1), .Byte(Byte_1),
    .WriteReg(WriteReg_1));
  or or_2 (isSATequalPC, comparator_1_eq, ForceStop);
  D_Flip_Flop d_ff_2 (.D(d_ff_1_q), .clk(in_2), .Q(d_ff_2_q));  // open: Qn, preset, reset
  SaturationCounter saturationcounter_1 (
    .Start(in_1), .Upcnt(Satu_1), .Downcnt(not_2_out), .t1(saturationcounter_1_t1));  // open: clk, t0
  or or_3 (ForceStop, d_ff_1_q, d_ff_2_q);
  not not_4 (SatuBit, saturationcounter_1_t1);
  Multiplexer #(.select(2), .width(32)) multiplexer_6 (
    .in0(PC4_1), .in1(adder_3_out), .in2(res_1), .in3({PC_1[31:28], ADD_1, 2'b00}), .out(nPC),
    .sel(PCcontrol_1));
  BigBuffer bigbuffer_3 (
    .In32_1({INS_1, ADD_1}), .In32_2(PC4_1), .In32_3(rtdata_1), .In32_4(res_1), .In32_5(PC_1),
    .In1_1(isRes_1), .In1_2(isJAL_1), .In1_3(isWriteRD_1), .In1_4(syscall_1), .In4_1(Byte_1),
    .In1_6(WriteReg_1), .In2_1(PCcontrol_1), .clk(in_2), .stop(isSATequalPC), .Out32_1({INS_2, ADD_2}),
    .Out32_2(PC4_2), .Out32_3(rtdata_2), .Out32_4(res_2), .Out32_5(PC_2), .Out1_1(isRes_2), .Out1_2(isJAL_2),
    .Out1_3(isWriteRD_2), .Out1_4(syscall_2), .Out4_1(Byte_2), .Out1_6(WriteReg_2), .Out2_1(PCcontrol_2));  // open: In16_2, In1_7, In1_8, In1_9, In1_10, In1_11, Out16_2, Out1_7, Out1_8, Out1_9, Out1_10, Out1_11
  // mem DataMem: pin names not known; wires that end beside it: res_2, Byte_2, rtdata_2, in_2, DataMem_p5
  Multiplexer #(.width(32)) multiplexer_7 (.in0(DataMem_p5), .in1(res_2), .out(writedata_2), .sel(isRes_2));
  BigBuffer bigbuffer_4 (
    .In32_1({INS_2, ADD_2}), .In32_2(PC4_2), .In32_3(writedata_2), .In32_4(nPC), .In1_1(isRes_2),
    .In1_2(isJAL_2), .In1_3(isWriteRD_2), .In1_4(syscall_2), .In4_1(Byte_2), .In1_6(WriteReg_2), .clk(in_2),
    .Out32_1({INS_3, ADD_3}), .Out32_2(PC4_3), .Out32_3(writedata_3), .Out32_4(nPC_1), .Out1_1(isRes_3),
    .Out1_2(isJAL_3), .Out1_3(isWriteRD_3), .Out1_4(syscall_3), .Out4_1(Byte_3), .Out1_6(WriteReg_3));  // open: In32_5, In16_2, In1_7, In1_8, In1_9, In1_10, In1_11, In2_1, stop, Out32_5, Out16_2, Out1_7, Out1_8, Out1_9, Out1_10, Out1_11, Out2_1

  // Other names for the same wires on the sheet: func_1[5:0] = ADD_1[5:0]; imm_1[15:0] = ADD_1[15:0];
  //   INS_1[25:0] = ADD_1; sa_1[4:0] = ADD_1[10:6]; rd_1[4:0] = ADD_1[15:11]; rt_1[4:0] = ADD_1[20:16];
  //   rs_1[4:0] = ADD_1[25:21]; func[5:0] = ADD[5:0]; imm[15:0] = ADD[15:0]; INS[25:0] = ADD; sa[4:0] = ADD[10:6];
  //   rd[4:0] = ADD[15:11]; rt[4:0] = ADD[20:16]; rs[4:0] = ADD[25:21]; OP[5:0] = INS; imm_0[15:0] = ADD_0[15:0];
  //   INS_0[25:0] = ADD_0; OP_0[5:0] = INS_0; OP_1[5:0] = INS_1; func_2[5:0] = ADD_2[5:0]; imm_2[15:0] = ADD_2[15:0];
  //   INS_2[25:0] = ADD_2; sa_2[4:0] = ADD_2[10:6]; rd_2[4:0] = ADD_2[15:11]; rt_2[4:0] = ADD_2[20:16];
  //   rs_2[4:0] = ADD_2[25:21]; OP_2[5:0] = INS_2; func_3[5:0] = ADD_3[5:0]; imm_3[15:0] = ADD_3[15:0];
  //   INS_3[25:0] = ADD_3; sa_3[4:0] = ADD_3[10:6]; rd_3[4:0] = ADD_3[15:11]; rt_3[4:0] = ADD_3[20:16];
  //   rs_3[4:0] = ADD_3[25:21]; OP_3[5:0] = INS_3; EXCLK = in_2; IDCLK = in_2; IFCLK = in_2; MEMCLK = in_2;
  //   pipelineCLK = in_2; WBCLK = in_2; START_CPU = in_1; stop = isSATequalPC

  // Notes on the sheet:
  //   SAT PC Control
  //   PC Control
  //   satPC v npc age barabar isSATequlPC = 1
  //   dar do ta clock avval hatman bayad isSatequalPC = 1
  //   agar dar clk i npc != satPC dar clk i isSatequalPPc = 0 va dar clk i+1, i+2 stop = 1 is SATequlPC = 1
endmodule

module BigBuffer (
  input  [31:0] In32_1,
  input  [31:0] In32_2,
  input  [31:0] In32_3,
  input  [31:0] In32_4,
  input  [31:0] In32_5,
  input  [31:0] In16_2,
  input  In1_1,
  input  In1_2,
  input  In1_3,
  input  In1_4,
  input  [3:0] In4_1,
  input  In1_6,
  input  In1_7,
  input  In1_8,
  input  In1_9,
  input  In1_10,
  input  In1_11,
  input  [1:0] In2_1,
  input  clk,
  input  stop,
  output [31:0] Out32_1,
  output [31:0] Out32_2,
  output [31:0] Out32_3,
  output [31:0] Out32_4,
  output [31:0] Out32_5,
  output [31:0] Out16_2,
  output Out1_1,
  output Out1_2,
  output Out1_3,
  output Out1_4,
  output [3:0] Out4_1,
  output Out1_6,
  output Out1_7,
  output Out1_8,
  output Out1_9,
  output Out1_10,
  output Out1_11,
  output [1:0] Out2_1
);

  wire CLK_t, not_1_out;

  not not_1 (not_1_out, stop);
  and and_1 (CLK_t, clk, not_1_out);
  Register #(.width(32)) register_1 (.D(In32_1), .clk(CLK_t), .Q(Out32_1));  // open: en, clr
  Register #(.width(32)) register_2 (.D(In32_2), .clk(CLK_t), .Q(Out32_2));  // open: en, clr
  Register #(.width(32)) register_3 (.D(In32_3), .clk(CLK_t), .Q(Out32_3));  // open: en, clr
  Register #(.width(32)) register_4 (.D(In32_4), .clk(CLK_t), .Q(Out32_4));  // open: en, clr
  Register #(.width(32)) register_5 (.D(In32_5), .clk(CLK_t), .Q(Out32_5));  // open: en, clr
  Register #(.width(32)) register_6 (.D(In16_2), .clk(CLK_t), .Q(Out16_2));  // open: en, clr
  Register #(.width(1)) register_7 (.D(In1_1), .clk(CLK_t), .Q(Out1_1));  // open: en, clr
  Register #(.width(1)) register_8 (.D(In1_2), .clk(CLK_t), .Q(Out1_2));  // open: en, clr
  Register #(.width(1)) register_9 (.D(In1_3), .clk(CLK_t), .Q(Out1_3));  // open: en, clr
  Register #(.width(1)) register_10 (.D(In1_4), .clk(CLK_t), .Q(Out1_4));  // open: en, clr
  Register #(.width(4)) register_11 (.D(In4_1), .clk(CLK_t), .Q(Out4_1));  // open: en, clr
  Register #(.width(1)) register_12 (.D(In1_6), .clk(CLK_t), .Q(Out1_6));  // open: en, clr
  Register #(.width(1)) register_13 (.D(In1_7), .clk(CLK_t), .Q(Out1_7));  // open: en, clr
  Register #(.width(1)) register_14 (.D(In1_8), .clk(CLK_t), .Q(Out1_8));  // open: en, clr
  Register #(.width(1)) register_15 (.D(In1_9), .clk(CLK_t), .Q(Out1_9));  // open: en, clr
  Register #(.width(1)) register_16 (.D(In1_10), .clk(CLK_t), .Q(Out1_10));  // open: en, clr
  Register #(.width(1)) register_17 (.D(In1_11), .clk(CLK_t), .Q(Out1_11));  // open: en, clr
  Register #(.width(2)) register_18 (.D(In2_1), .clk(CLK_t), .Q(Out2_1));  // open: en, clr
endmodule

module SaturationCounter (
  input  Start,
  input  Upcnt,
  input  Downcnt,
  input  clk,
  output t0,
  output t1
);

  wire and_1_out, and_2_out, and_3_out, and_4_out, decoder_1_out0, decoder_1_out3, decoder_2_out1,
       decoder_2_out2, nor_1_out, nor_2_out, or_1_out;

  Decoder #(.enable("false"), .select(2)) decoder_1 (
    .out0(decoder_1_out0), .out3(decoder_1_out3), .sel({t1, t0}));  // open: out1, out2
  and and_1 (and_1_out, Downcnt, decoder_1_out0);
  and and_2 (and_2_out, Upcnt, decoder_1_out3);
  nor nor_1 (nor_1_out, Upcnt, Downcnt);
  Decoder #(.enable("false"), .select(2)) decoder_2 (
    .out1(decoder_2_out1), .out2(decoder_2_out2), .sel({t1, t0}));  // open: out0, out3
  nor nor_2 (nor_2_out, and_1_out, and_2_out, nor_1_out);
  and and_3 (and_3_out, Upcnt, decoder_2_out1);
  and and_4 (and_4_out, decoder_2_out2, Downcnt);
  or or_1 (or_1_out, and_3_out, and_4_out);
  T_Flip_Flop t_ff_1 (.T(nor_2_out), .clk(clk), .Q(t0), .preset(Start));  // open: Qn, reset
  T_Flip_Flop t_ff_2 (.T(or_1_out), .clk(clk), .Q(t1), .preset(Start));  // open: Qn, reset

  // Other names for the same wires on the sheet: down = Downcnt; up = Upcnt
endmodule
