// Logisim project fiveCounter.circ as structural Verilog: 1 circuit, main circuit fiveCounter
module fiveCounter (
  input  Start,
  input  Clk,
  input  miss,
  output S_IF,
  output S_ID,
  output S_EX,
  output S_MEM,
  output S_WB
);

  wire IN_MEM, IN_WB, nor_1_out, not_1_out;

  not not_1 (not_1_out, miss);
  D_Flip_Flop d_ff_1 (.D(S_WB), .clk(Clk), .Q(S_IF), .preset(Start));  // open: Qn, reset
  D_Flip_Flop d_ff_2 (.D(S_IF), .clk(Clk), .Q(S_ID), .reset(Start));  // open: Qn, preset
  D_Flip_Flop d_ff_3 (.D(S_ID), .clk(Clk), .Q(S_EX), .reset(Start));  // open: Qn, preset
  D_Flip_Flop d_ff_4 (.D(IN_MEM), .clk(Clk), .Q(S_MEM), .reset(Start));  // open: Qn, preset
  D_Flip_Flop d_ff_5 (.D(IN_WB), .clk(Clk), .Q(S_WB), .reset(Start));  // open: Qn, preset
  or or_1 (IN_MEM, S_EX, nor_1_out);
  nor nor_1 (nor_1_out, S_IF, S_ID, S_EX, S_MEM, S_WB, not_1_out);
  and and_1 (IN_WB, S_MEM, not_1_out);
endmodule
