// Logisim project improvedMemory.circ as structural Verilog: 1 circuit, main circuit improvedMemory
// writeData
module improvedMemory (
  input  [31:0] MemAddress,
  input  [31:0] MemWriteData,
  input  [3:0] MemWriteMask,
  input  Clk
);

  // memDelayed memdelayed_1: pin names not known; wires that end beside it: MemAddress, MemWriteMask, MemWriteData, Clk

  // Other names for the same wires on the sheet: address[31:0] = MemAddress; word[1:0] = MemAddress[1:0];
  //   set[1:0] = MemAddress[3:2]; tag[9:0] = MemAddress[13:4]; writeData[31:0] = MemWriteData;
  //   writeMask[3:0] = MemWriteMask
endmodule
